# Fritzing sketch LightLight (saved by Fritzing 0.9.2b)
stripboards: 1

parts:
  TRINKET1 = Trinket 3V
  LED2 = RGB LED - (4 legs) [package="5 mm [THT]"]
  R1 = PHOTOCELL [package=photocell]
  JP1 = Header 1 [package=1x01_offset]
  JP2 = Header 1 [package=1x01_offset]
  JP3 = Header 1 [package=1x01_offset]
  JP4 = Header 1 [package=1x01_offset]
  JP5 = Header 1 [package=1x01_offset]
  JP6 = Header 1 [package=1x01_offset]
  R2 = Resistor [tolerance=±5% resistance=220 package=THT]

nets:
  N1: TRINKET1.no_name_yet#1, LED2.green_cathode, R1.P$2, JP2.1, JP4.1
  N2: TRINKET1.no_name_yet#2, LED2.common_anode, JP5.1
  N3: TRINKET1.no_name_yet#7, R2.Pin_1
  N4: TRINKET1.no_name_yet#9, LED2.blue_cathode, JP3.1
  N5: LED2.red_cathode, JP6.1
  N6: R1.P$1, JP1.1, R2.Pin_0

custom parts:
  Trinket 3V: Adafruit Trinket 3V
