# Fritzing sketch LightSound (saved by Fritzing 0.9.2b)
stripboards: 1

parts:
  TRINKET1 = Trinket 3V
  R1 = PHOTOCELL [package=photocell]
  JP1 = Header 1 [package=1x01_offset]
  JP2 = Header 1 [package=1x01_offset]
  JP3 = Header 1 [package=1x01_offset]
  JP4 = Header 1 [package=1x01_offset]
  J1 = Piezo Speaker
  R3 = Resistor [tolerance=±5% resistance=220 package=THT]

nets:
  N1: TRINKET1.no_name_yet#1, R1.P$2, JP2.1
  N2: TRINKET1.no_name_yet#2, JP4.1, J1.pin1, R3.Pin_1
  N3: TRINKET1.no_name_yet#7, R1.P$1, JP1.1, R3.Pin_0
  N4: TRINKET1.no_name_yet#9, JP3.1, J1.pin2

custom parts:
  Trinket 3V: Adafruit Trinket 3V
